// Logisim project Complete TSC.circ as structural Verilog: 15 circuits, main circuit MUX
module FULL_ADD (
  input  a,
  input  b,
  input  c,
  output SOP_SUM,
  output SOP_COUT
);

  wire and_1_out, and_2_out, and_3_out, and_4_out, and_5_out, and_6_out, and_7_out, and_8_out;

  and and_1 (and_1_out, ~a, ~b, c);  // AND_Gate
  and and_2 (and_2_out, ~a, b, ~c);  // AND_Gate
  and and_3 (and_3_out, a, ~b, ~c);  // AND_Gate
  and and_4 (and_4_out, a, b, c);
  and and_5 (and_5_out, ~a, b, c);  // AND_Gate
  and and_6 (and_6_out, a, ~b, c);  // AND_Gate
  and and_7 (and_7_out, a, b, ~c);  // AND_Gate
  and and_8 (and_8_out, a, b, c);
  or or_1 (SOP_SUM, and_1_out, and_2_out, and_3_out, and_4_out);
  or or_2 (SOP_COUT, and_5_out, and_6_out, and_7_out, and_8_out);
endmodule

module MUX (
  input  a,
  input  b,
  input  s,
  output SOP_O
);

  wire and_1_out, and_2_out, and_3_out, and_4_out;

  and and_1 (and_1_out, a, b, ~s);  // AND_Gate
  and and_2 (and_2_out, a, b, s);
  and and_3 (and_3_out, ~a, b, s);  // AND_Gate
  and and_4 (and_4_out, a, ~b, ~s);  // AND_Gate
  or or_1 (SOP_O, and_3_out, and_4_out, and_1_out, and_2_out);
endmodule

module ALU_Bit (
  input  BUS_1i,
  input  BUS1i_1,
  input  BUS_1i_1,
  input  BUS_2i,
  input  ADD,
  input  SUB,
  input  AND,
  input  OR,
  input  NOT,
  input  TCP,
  input  SHL,
  input  SHR,
  input  TRA1,
  input  CIN,
  output COUT,
  output BUS3
);

  wire and_1_out, and_2_out, and_3_out, and_4_out, and_5_out, and_6_out, and_7_out, and_8_out, and_9_out,
       AND_OP_out, FULL_ADDER_sop_sum, MUX_sop_o, not_1_out, not_2_out, or_1_out, or_2_out;

  not not_1 (not_1_out, BUS_2i);
  or or_1 (or_1_out, SUB, TCP);
  MUX MUX (.a(BUS_2i), .b(not_1_out), .s(or_1_out), .SOP_O(MUX_sop_o));
  FULL_ADD FULL_ADDER (.a(BUS_1i), .b(MUX_sop_o), .c(CIN), .SOP_SUM(FULL_ADDER_sop_sum), .SOP_COUT(COUT));
  and and_1 (and_1_out, ADD, FULL_ADDER_sop_sum);
  and and_2 (and_2_out, FULL_ADDER_sop_sum, TCP);
  and and_3 (and_3_out, FULL_ADDER_sop_sum, SUB);
  and AND_OP (AND_OP_out, BUS_1i, BUS_2i);
  not not_2 (not_2_out, BUS_2i);
  and and_4 (and_4_out, not_2_out, NOT);
  and and_5 (and_5_out, BUS_1i_1, SHL);
  and and_6 (and_6_out, BUS1i_1, SHR);
  and and_7 (and_7_out, BUS_1i, TRA1);
  and and_8 (and_8_out, AND_OP_out, AND);
  or or_2 (or_2_out, BUS_1i, BUS_2i);
  and and_9 (and_9_out, or_2_out, OR);
  or or_3 (BUS3, and_4_out, and_5_out, and_6_out, and_1_out, and_3_out, and_2_out, and_7_out, and_8_out, and_9_out);
endmodule

module ComR (
  input  CIN,
  input  BUS_1i,
  input  BUS_2i,
  input  OR,
  input  ADD,
  input  SUB,
  input  NOT,
  input  TRA,
  input  AND,
  input  SHL,
  input  TCP,
  input  BUS_1i_1,
  input  SHR,
  input  BUS1i_1,
  output BUS3
);

  wire and_1_out, and_2_out, and_3_out, and_4_out, and_5_out, and_6_out, and_7_out, and_8_out, and_9_out,
       and_10_out, and_11_out, and_12_out, and_13_out, and_14_out, and_15_out, and_16_out, and_17_out,
       and_18_out, and_19_out, and_20_out, or_1_out;

  and and_1 (and_1_out, BUS_1i, AND);
  and and_2 (and_2_out, BUS_2i, AND);
  and and_3 (and_3_out, SHL, BUS_1i_1);
  and and_4 (and_4_out, SHR, BUS1i_1);
  and and_5 (and_5_out, and_1_out, and_2_out);
  and and_6 (and_6_out, BUS_1i, OR);
  and and_7 (and_7_out, BUS_2i, OR);
  or or_1 (or_1_out, and_6_out, and_7_out);
  and and_8 (and_8_out, NOT, ~BUS_2i);  // AND_Gate
  and and_9 (and_9_out, TRA, BUS_1i);
  and and_10 (and_10_out, TCP, ~BUS_2i);  // AND_Gate
  and and_11 (and_11_out, TCP, CIN);
  and and_12 (and_12_out, ADD, BUS_1i);
  and and_13 (and_13_out, ADD, BUS_2i);
  and and_14 (and_14_out, ADD, CIN);
  and and_15 (and_15_out, and_10_out, and_11_out);
  and and_16 (and_16_out, and_12_out, and_13_out, and_14_out);
  and and_17 (and_17_out, SUB, BUS_1i);
  and and_18 (and_18_out, SUB, ~BUS_2i);  // AND_Gate
  and and_19 (and_19_out, SUB, CIN);
  and and_20 (and_20_out, and_17_out, and_18_out, and_19_out);
  or or_2 (BUS3, and_20_out, and_16_out, and_15_out, and_9_out, and_8_out, or_1_out, and_5_out, and_3_out, and_4_out);
endmodule

module ComL (
  input  SUB,
  input  TCP,
  input  BUS_1i,
  input  BUS_2i,
  output out_5,
  output out_6,
  output out_7
);

  or or_1 (out_5, SUB, TCP);
  and and_1 (out_7, ~TCP, BUS_1i);  // AND_Gate

  assign out_6 = BUS_2i;
endmodule

module ALU (
  input  ADD,
  input  SUB,
  input  AND,
  input  OR,
  input  NOT,
  input  TCP,
  input  SHL,
  input  SHR,
  input  TRA1,
  input  [15:0] BUS1,
  input  [15:0] BUS2,
  output COUT,
  output out_13,
  output [15:0] out_14
);

  wire alu_bit_1_cout, alu_bit_2_cout, alu_bit_3_cout, alu_bit_4_cout, alu_bit_5_cout, alu_bit_6_cout,
       alu_bit_7_cout, alu_bit_8_cout, alu_bit_9_cout, alu_bit_10_cout, alu_bit_11_cout, alu_bit_12_cout,
       alu_bit_13_cout, alu_bit_14_cout, alu_bit_15_cout, or_1_out, or_2_out;

  or or_1 (or_1_out, SUB, AND);
  ALU_Bit alu_bit_1 (
    .BUS_1i(BUS1[0]), .BUS1i_1(BUS1[1]), .BUS_1i_1(1'b0), .BUS_2i(BUS2[0]), .ADD(ADD), .SUB(SUB), .AND(AND),
    .OR(OR), .NOT(NOT), .TCP(TCP), .SHL(SHL), .SHR(SHR), .TRA1(TRA1), .CIN(or_1_out), .COUT(alu_bit_1_cout),
    .BUS3(out_14[0]));
  ALU_Bit alu_bit_2 (
    .BUS_1i(BUS1[4]), .BUS1i_1(BUS1[5]), .BUS_1i_1(BUS1[3]), .BUS_2i(BUS2[4]), .ADD(ADD), .SUB(SUB),
    .AND(AND), .OR(OR), .NOT(NOT), .TCP(TCP), .SHL(SHL), .SHR(SHR), .TRA1(TRA1), .CIN(alu_bit_13_cout),
    .COUT(alu_bit_2_cout), .BUS3(out_14[4]));
  ALU_Bit alu_bit_3 (
    .BUS_1i(BUS1[8]), .BUS1i_1(BUS1[9]), .BUS_1i_1(BUS1[7]), .BUS_2i(BUS2[8]), .ADD(ADD), .SUB(SUB),
    .AND(AND), .OR(OR), .NOT(NOT), .TCP(TCP), .SHL(SHL), .SHR(SHR), .TRA1(TRA1), .CIN(alu_bit_14_cout),
    .COUT(alu_bit_3_cout), .BUS3(out_14[8]));
  ALU_Bit alu_bit_4 (
    .BUS_1i(BUS1[12]), .BUS1i_1(BUS1[13]), .BUS_1i_1(BUS1[11]), .BUS_2i(BUS2[12]), .ADD(ADD), .SUB(SUB),
    .AND(AND), .OR(OR), .NOT(NOT), .TCP(TCP), .SHL(SHL), .SHR(SHR), .TRA1(TRA1), .CIN(alu_bit_15_cout),
    .COUT(alu_bit_4_cout), .BUS3(out_14[12]));
  ALU_Bit alu_bit_5 (
    .BUS_1i(BUS1[1]), .BUS1i_1(BUS1[2]), .BUS_1i_1(BUS1[0]), .BUS_2i(BUS2[1]), .ADD(ADD), .SUB(SUB),
    .AND(AND), .OR(OR), .NOT(NOT), .TCP(TCP), .SHL(SHL), .SHR(SHR), .TRA1(TRA1), .CIN(alu_bit_1_cout),
    .COUT(alu_bit_5_cout), .BUS3(out_14[1]));
  ALU_Bit alu_bit_6 (
    .BUS_1i(BUS1[5]), .BUS1i_1(BUS1[6]), .BUS_1i_1(BUS1[4]), .BUS_2i(BUS2[5]), .ADD(ADD), .SUB(SUB),
    .AND(AND), .OR(OR), .NOT(NOT), .TCP(TCP), .SHL(SHL), .SHR(SHR), .TRA1(TRA1), .CIN(alu_bit_2_cout),
    .COUT(alu_bit_6_cout), .BUS3(out_14[5]));
  ALU_Bit alu_bit_7 (
    .BUS_1i(BUS1[9]), .BUS1i_1(BUS1[10]), .BUS_1i_1(BUS1[8]), .BUS_2i(BUS2[9]), .ADD(ADD), .SUB(SUB),
    .AND(AND), .OR(OR), .NOT(NOT), .TCP(TCP), .SHL(SHL), .SHR(SHR), .TRA1(TRA1), .CIN(alu_bit_3_cout),
    .COUT(alu_bit_7_cout), .BUS3(out_14[9]));
  ALU_Bit alu_bit_8 (
    .BUS_1i(BUS1[13]), .BUS1i_1(BUS1[14]), .BUS_1i_1(BUS1[12]), .BUS_2i(BUS2[13]), .ADD(ADD), .SUB(SUB),
    .AND(AND), .OR(OR), .NOT(NOT), .TCP(TCP), .SHL(SHL), .SHR(SHR), .TRA1(TRA1), .CIN(alu_bit_4_cout),
    .COUT(alu_bit_8_cout), .BUS3(out_14[13]));
  ALU_Bit alu_bit_9 (
    .BUS_1i(BUS1[14]), .BUS1i_1(BUS1[15]), .BUS_1i_1(BUS1[13]), .BUS_2i(BUS2[14]), .ADD(ADD), .SUB(SUB),
    .AND(AND), .OR(OR), .NOT(NOT), .TCP(TCP), .SHL(SHL), .SHR(SHR), .TRA1(TRA1), .CIN(alu_bit_8_cout),
    .COUT(alu_bit_9_cout), .BUS3(out_14[14]));
  ALU_Bit alu_bit_10 (
    .BUS_1i(BUS1[2]), .BUS1i_1(BUS1[3]), .BUS_1i_1(BUS1[1]), .BUS_2i(BUS2[2]), .ADD(ADD), .SUB(SUB),
    .AND(AND), .OR(OR), .NOT(NOT), .TCP(TCP), .SHL(SHL), .SHR(SHR), .TRA1(TRA1), .CIN(alu_bit_5_cout),
    .COUT(alu_bit_10_cout), .BUS3(out_14[2]));
  ALU_Bit alu_bit_11 (
    .BUS_1i(BUS1[6]), .BUS1i_1(BUS1[7]), .BUS_1i_1(BUS1[5]), .BUS_2i(BUS2[6]), .ADD(ADD), .SUB(SUB),
    .AND(AND), .OR(OR), .NOT(NOT), .TCP(TCP), .SHL(SHL), .SHR(SHR), .TRA1(TRA1), .CIN(alu_bit_6_cout),
    .COUT(alu_bit_11_cout), .BUS3(out_14[6]));
  ALU_Bit alu_bit_12 (
    .BUS_1i(BUS1[10]), .BUS1i_1(BUS1[11]), .BUS_1i_1(BUS1[9]), .BUS_2i(BUS2[10]), .ADD(ADD), .SUB(SUB),
    .AND(AND), .OR(OR), .NOT(NOT), .TCP(TCP), .SHL(SHL), .SHR(SHR), .TRA1(TRA1), .CIN(alu_bit_7_cout),
    .COUT(alu_bit_12_cout), .BUS3(out_14[10]));
  ALU_Bit alu_bit_13 (
    .BUS_1i(BUS1[3]), .BUS1i_1(BUS1[4]), .BUS_1i_1(BUS1[2]), .BUS_2i(BUS2[3]), .ADD(ADD), .SUB(SUB),
    .AND(AND), .OR(OR), .NOT(NOT), .TCP(TCP), .SHL(SHL), .SHR(SHR), .TRA1(TRA1), .CIN(alu_bit_10_cout),
    .COUT(alu_bit_13_cout), .BUS3(out_14[3]));
  ALU_Bit alu_bit_14 (
    .BUS_1i(BUS1[7]), .BUS1i_1(BUS1[8]), .BUS_1i_1(BUS1[6]), .BUS_2i(BUS2[7]), .ADD(ADD), .SUB(SUB),
    .AND(AND), .OR(OR), .NOT(NOT), .TCP(TCP), .SHL(SHL), .SHR(SHR), .TRA1(TRA1), .CIN(alu_bit_11_cout),
    .COUT(alu_bit_14_cout), .BUS3(out_14[7]));
  ALU_Bit alu_bit_15 (
    .BUS_1i(BUS1[11]), .BUS1i_1(BUS1[12]), .BUS_1i_1(BUS1[10]), .BUS_2i(BUS2[11]), .ADD(ADD), .SUB(SUB),
    .AND(AND), .OR(OR), .NOT(NOT), .TCP(TCP), .SHL(SHL), .SHR(SHR), .TRA1(TRA1), .CIN(alu_bit_12_cout),
    .COUT(alu_bit_15_cout), .BUS3(out_14[11]));
  ALU_Bit alu_bit_16 (
    .BUS_1i(BUS1[15]), .BUS1i_1(1'b0), .BUS_1i_1(BUS1[14]), .BUS_2i(BUS2[15]), .ADD(ADD), .SUB(SUB),
    .AND(AND), .OR(OR), .NOT(NOT), .TCP(TCP), .SHL(SHL), .SHR(SHR), .TRA1(TRA1), .CIN(alu_bit_9_cout),
    .COUT(COUT), .BUS3(out_14[15]));
  not not_1 (out_13, or_2_out);
  or or_2 (or_2_out, out_14[15], out_14[14], out_14[13], out_14[12], out_14[11], out_14[10], out_14[9], out_14[8], out_14[7], out_14[6], out_14[5], out_14[4], out_14[3], out_14[2], out_14[1], out_14[0]);

  // Other names for the same wires on the sheet: B1B0 = BUS1[0]; B1B1 = BUS1[1]; B1B2 = BUS1[2]; B1B3 = BUS1[3];
  //   B1B4 = BUS1[4]; B1B5 = BUS1[5]; B1B6 = BUS1[6]; B1B7 = BUS1[7]; B1B8 = BUS1[8]; B1B9 = BUS1[9];
  //   B1B10 = BUS1[10]; B1B11 = BUS1[11]; B1B12 = BUS1[12]; B1B13 = BUS1[13]; B1B14 = BUS1[14]; B1B15 = BUS1[15];
  //   B2B0 = BUS2[0]; B2B1 = BUS2[1]; B2B2 = BUS2[2]; B2B3 = BUS2[3]; B2B4 = BUS2[4]; B2B5 = BUS2[5]; B2B6 = BUS2[6];
  //   B2B7 = BUS2[7]; B2B8 = BUS2[8]; B2B9 = BUS2[9]; B2B10 = BUS2[10]; B2B11 = BUS2[11]; B2B12 = BUS2[12];
  //   B2B13 = BUS2[13]; B2B14 = BUS2[14]; B2B15 = BUS2[15]; B0OUT = out_14[0]; B1OUT = out_14[1]; B2OUT = out_14[2];
  //   B3OUT = out_14[3]; B4OUT = out_14[4]; B5OUT = out_14[5]; B6OUT = out_14[6]; B7OUT = out_14[7];
  //   B8OUT = out_14[8]; B9OUT = out_14[9]; B10OUT = out_14[10]; B11OUT = out_14[11]; B12OUT = out_14[12];
  //   B13OUT = out_14[13]; B14OUT = out_14[14]; B15OUT = out_14[15]
endmodule

module ALU_TEST (
  input  [15:0] in_1,
  input  [15:0] in_2,
  input  ADD,
  input  SUB,
  input  AND,
  input  OR,
  input  NOT,
  input  TCP,
  input  SHL,
  input  SHR,
  input  TRA1,
  output out_12,
  output [15:0] out_13
);

  wire alu_1_out_13;

  // Probe on in_1
  // Probe on in_2
  ALU alu_1 (
    .ADD(ADD), .SUB(SUB), .AND(AND), .OR(OR), .NOT(NOT), .TCP(TCP), .SHL(SHL), .SHR(SHR), .TRA1(TRA1),
    .COUT(out_12), .BUS1(in_1), .BUS2(in_2), .out_14(out_13), .out_13(alu_1_out_13));
  // Probe on out_13
endmodule

module Datapath (
  input  [15:0] in_1,
  input  CLRMEM,
  input  [15:0] in_3,
  input  in_4,
  input  START,
  input  DATA,
  output [15:0] out_7,
  output [15:0] out_8,
  output [15:0] out_9,
  output [15:0] out_10,
  output out_11,
  output out_12
);

  wire _1toB2, ADD, AND, and_1_out, and_14_out, and_15_out, and_16_out, and_17_out, and_18_out, and_19_out,
       and_20_out, and_21_out, B3toG0, B3toG1, B3toG2, B3toG3, B3toGPR2, B3toGPRD, B3toGPRT, B3toIR, B3toMAR,
       B3toMBR, B3toPC, bMicro, button_1_out, CC0, CC1, CC2, CC3, CC4, CC5, CC6, CLK, ERROR, G0toB1, G0toB2,
       G1toB1, G1toB2, G2toB1, G2toB2, G3toB1, G3toB2, GPRStoB1, GPRStoB2, GPRTtoB1, GPRTtoB2, INPUT, IR0P,
       IR1P, IR2P, IR3P, IR4P, IR5P, MBRtoB1, MEMtoMBR, mS0, mS1, n2x4dec_1_q0, n2x4dec_1_q1, n2x4dec_1_q2,
       n2x4dec_1_q3, n2x4dec_2_q0, n2x4dec_2_q1, n2x4dec_2_q2, n2x4dec_2_q3, n2x4dec_3_q0, n2x4dec_3_q1,
       n2x4dec_3_q2, n2x4dec_3_q3, n2x4dec_4_q0, n2x4dec_4_q1, n2x4dec_4_q2, n2x4dec_4_q3, n2x4dec_5_q0,
       n2x4dec_5_q1, n2x4dec_5_q2, n2x4dec_5_q3, n2x4dec_6_q0, n2x4dec_6_q1, n2x4dec_6_q2, n2x4dec_6_q3, NOT,
       not_1_out, not_2_out, not_3_out, OR, or_1_out, OUTPUT, PCtoB1, SHL, SHR, SIMMtoB2, SUB,
       syncbutton_1_out, syncbutton_2_out, TARGETtoB1, TCP, TRA1, UPIMMtoB1, USIMMtoB2, WRITE;
  wire [0:0] register_11_q;
  wire [3:0] register_1_q_2, register_1_q_3;
  wire [7:0] adder_1_out, adder_2_out, MicroAddress, microMAR, multiplexer_3_out, register_1_q;
  wire [15:0] IR, MAR, MBR, multiplexer_1_out, multiplexer_2_out, PC, R0, R1, R2, R3, rom_1_data;
  wire [31:0] rom_2_data;

  // Probe on out_10
  Clock #(.highDuration(100), .lowDuration(100)) clock_1 (.out(CLK));
  Hex_Digit_Display hex_digit_display_1 (.value(register_1_q_3));  // open: dp
  Register register_1 (.D(out_10), .Q({register_1_q_3, register_1_q_2, register_1_q}), .CLR(in_4), .CLK(OUTPUT));
  Multiplexer #(.width(16)) multiplexer_1 (
    .in0(out_10), .in1(in_1), .out(multiplexer_1_out), .sel(button_1_out));  // open: en
  Button button_1 (.out(button_1_out));
  Register register_2 (.D(out_10), .Q(MAR), .CLR(in_4), .CLK(B3toMAR));
  // Probe on multiplexer_2_out
  Multiplexer #(.width(16)) multiplexer_2 (
    .in0(out_10), .in1(out_9), .out(multiplexer_2_out), .sel(MEMtoMBR));  // open: en
  Hex_Digit_Display hex_digit_display_2 (.value(register_1_q_2));  // open: dp
  Hex_Digit_Display hex_digit_display_3 (.value(register_1_q[7:4]));  // open: dp
  // Probe on MAR
  Register register_3 (.D(multiplexer_2_out), .Q(MBR), .CLR(in_4), .CLK(B3toMBR));
  // Probe on microMAR
  Hex_Digit_Display hex_digit_display_4 (.value(register_1_q[3:0]));  // open: dp
  LED led_1 (.in(OUTPUT));
  // Probe on PC
  Register register_4 (.D(multiplexer_1_out), .Q(PC), .CLR(in_4), .CLK(and_1_out));
  and and_1 (and_1_out, B3toPC, ~button_1_out);  // AND_Gate
  not not_1 (not_1_out, WRITE);
  // Probe on MBR
  Hex_Digit_Display hex_digit_display_5 (.value(out_10[15:12]));  // open: dp
  Hex_Digit_Display hex_digit_display_6 (.value(out_10[11:8]));  // open: dp
  // Probe on PC
  // Probe on out_8
  // Probe on out_7
  // Probe on out_10
  // Probe on PC
  Hex_Digit_Display hex_digit_display_7 (.value(out_10[3:0]));  // open: dp
  Hex_Digit_Display hex_digit_display_8 (.value(out_10[7:4]));  // open: dp
  Tri_State_Buffer tri_state_buffer_1 (.in_1(PC), .out_3(out_8), .in_2(PCtoB1));
  RAM #(.addrWidth(16), .dataWidth(16), .bus("separate")) ram_1 (
    .addr(MAR), .din(MBR), .data(out_9), .str(not_1_out), .sel(1'b1), .clk(not_1_out), .ld(WRITE),
    .clr(CLRMEM));
  // Probe on MAR
  // Probe on MBR
  // Probe on IR
  Tri_State_Buffer tri_state_buffer_2 (.in_1(MBR), .out_3(out_8), .in_2(MBRtoB1));
  Hex_Digit_Display hex_digit_display_9 (.value(out_8[15:12]));  // open: dp
  // Probe on R0
  // Probe on R1
  // Probe on R2
  // Probe on R3
  Hex_Digit_Display hex_digit_display_10 (.value(out_8[11:8]));  // open: dp
  Hex_Digit_Display hex_digit_display_11 (.value(out_8[7:4]));  // open: dp
  not not_2 (not_2_out, INPUT);
  Hex_Digit_Display hex_digit_display_12 (.value(out_8[3:0]));  // open: dp
  Tri_State_Buffer tri_state_buffer_3 (.in_1(in_3), .out_3(out_8), .in_2(not_2_out));
  Hex_Digit_Display hex_digit_display_13 (.value(out_7[15:12]));  // open: dp
  Hex_Digit_Display hex_digit_display_14 (.value(out_7[11:8]));  // open: dp
  Tri_State_Buffer U_IMM (.in_1({{8{1'b0}}, IR[7:0]}), .out_3(out_7), .in_2(USIMMtoB2));
  Tri_State_Buffer S_IMM (.in_1({{9{IR[7]}}, IR[6:0]}), .out_3(out_7), .in_2(SIMMtoB2));
  Tri_State_Buffer UP_IMM (.in_1({IR[7:0], {8{1'b0}}}), .out_3(out_8), .in_2(UPIMMtoB1));
  Tri_State_Buffer TARGET (.in_1({PC[15:12], IR[11:0]}), .out_3(out_8), .in_2(TARGETtoB1));
  Tri_State_Buffer tri_state_buffer_4 (.in_1(R0), .out_3(out_8), .in_2(G0toB1));
  Tri_State_Buffer tri_state_buffer_5 (.in_1(R0), .out_3(out_7), .in_2(G0toB2));
  Tri_State_Buffer tri_state_buffer_6 (.in_1(R1), .out_3(out_8), .in_2(G1toB1));
  Tri_State_Buffer tri_state_buffer_7 (.in_1(R1), .out_3(out_7), .in_2(G1toB2));
  Tri_State_Buffer tri_state_buffer_8 (.in_1(R2), .out_3(out_8), .in_2(G2toB1));
  Tri_State_Buffer tri_state_buffer_9 (.in_1(R2), .out_3(out_7), .in_2(G2toB2));
  Tri_State_Buffer tri_state_buffer_10 (.in_1(R3), .out_3(out_8), .in_2(G3toB1));
  Tri_State_Buffer tri_state_buffer_11 (.in_1(R3), .out_3(out_7), .in_2(G3toB2));
  Tri_State_Buffer tri_state_buffer_12 (.in_1(16'h1), .out_3(out_7), .in_2(_1toB2));
  ALU alu_1 (
    .ADD(ADD), .SUB(SUB), .AND(AND), .OR(OR), .NOT(NOT), .TCP(TCP), .SHL(SHL), .SHR(SHR), .TRA1(TRA1),
    .COUT(out_11), .BUS1(out_8), .BUS2(out_7), .out_14(out_10), .out_13(out_12));
  Hex_Digit_Display hex_digit_display_15 (.value(out_7[3:0]));  // open: dp
  Hex_Digit_Display hex_digit_display_16 (.value(out_7[7:4]));  // open: dp
  Register register_5 (.D(out_10), .Q(R0), .CLR(in_4), .CLK(B3toG0));
  Register register_6 (.D(out_10), .Q(R1), .CLR(in_4), .CLK(B3toG1));
  Register register_7 (.D(out_10), .Q(R2), .CLR(in_4), .CLK(B3toG2));
  Register register_8 (.D(out_10), .Q(R3), .CLR(in_4), .CLK(B3toG3));
  // Probe on IR
  // Probe on R0
  // Probe on R1
  // Probe on R2
  // Probe on R3
  Register register_9 (.D(out_10), .Q(IR), .CLR(in_4), .CLK(B3toIR));
  _2x4Dec u_2x4dec_1 (
    .EN(B3toGPRT), .S(IR[9:8]), .Q0(n2x4dec_1_q0), .Q1(n2x4dec_1_q1), .Q2(n2x4dec_1_q2), .Q3(n2x4dec_1_q3));
  _2x4Dec u_2x4dec_2 (
    .EN(B3toGPRD), .S(IR[7:6]), .Q0(n2x4dec_2_q0), .Q1(n2x4dec_2_q1), .Q2(n2x4dec_2_q2), .Q3(n2x4dec_2_q3));
  _2x4Dec u_2x4dec_3 (
    .EN(GPRStoB2), .S(IR[11:10]), .Q0(n2x4dec_3_q0), .Q1(n2x4dec_3_q1), .Q2(n2x4dec_3_q2), .Q3(n2x4dec_3_q3));
  _2x4Dec u_2x4dec_4 (
    .EN(GPRTtoB2), .S(IR[9:8]), .Q0(n2x4dec_4_q0), .Q1(n2x4dec_4_q1), .Q2(n2x4dec_4_q2), .Q3(n2x4dec_4_q3));
  _2x4Dec u_2x4dec_5 (
    .EN(GPRStoB1), .S(IR[11:10]), .Q0(n2x4dec_5_q0), .Q1(n2x4dec_5_q1), .Q2(n2x4dec_5_q2), .Q3(n2x4dec_5_q3));
  _2x4Dec u_2x4dec_6 (
    .EN(GPRTtoB1), .S(IR[9:8]), .Q0(n2x4dec_6_q0), .Q1(n2x4dec_6_q1), .Q2(n2x4dec_6_q2), .Q3(n2x4dec_6_q3));
  and and_2 (B3toG0, n2x4dec_1_q0, n2x4dec_2_q0);
  and and_3 (B3toG1, n2x4dec_1_q1, n2x4dec_2_q1);
  and and_4 (B3toG2, n2x4dec_1_q2, B3toGPR2, n2x4dec_2_q2);
  and and_5 (B3toG3, n2x4dec_1_q3, n2x4dec_2_q3);
  and and_6 (G0toB2, n2x4dec_3_q0, n2x4dec_4_q0);
  and and_7 (G1toB2, n2x4dec_3_q1, n2x4dec_4_q1);
  and and_8 (G2toB2, n2x4dec_3_q2, n2x4dec_4_q2);
  and and_9 (G3toB2, n2x4dec_3_q3, n2x4dec_4_q3);
  and and_10 (G0toB1, n2x4dec_5_q0, n2x4dec_6_q0);
  and and_11 (G1toB1, n2x4dec_5_q1, n2x4dec_6_q1);
  and and_12 (G2toB1, n2x4dec_5_q2, n2x4dec_6_q2);
  and and_13 (G3toB1, n2x4dec_5_q3, n2x4dec_6_q3);
  SyncButton syncbutton_1 (.B(START), .CLK(CLK), .RESET(in_4), .OUT(syncbutton_1_out));
  SyncButton syncbutton_2 (.B(DATA), .CLK(CLK), .RESET(in_4), .OUT(syncbutton_2_out));
  or or_1 (or_1_out, out_10[15], out_12);
  and and_14 (and_14_out, CC3, ~out_12);  // AND_Gate
  and and_15 (and_15_out, CC4, out_12);
  and and_16 (and_16_out, CC5, ~out_10[15]);  // AND_Gate
  and and_17 (and_17_out, CC6, or_1_out);
  and and_18 (and_18_out, ~syncbutton_1_out, bMicro);  // AND_Gate
  and and_19 (and_19_out, ~syncbutton_1_out, CC1);  // AND_Gate
  and and_20 (and_20_out, CC2, ~syncbutton_2_out);  // AND_Gate
  Adder adder_1 (.a(microMAR), .b(8'h1), .out(adder_1_out), .cin(1'b0));  // open: cout
  or or_2 (mS1, syncbutton_1_out, CC1);
  or or_3 (mS0, and_18_out, and_19_out);
  or or_4 (bMicro, CC0, and_20_out, and_14_out, and_15_out, and_16_out, and_17_out);
  Multiplexer #(.select(2), .width(8), .enable("false")) multiplexer_3 (
    .in0(adder_1_out), .in1(MicroAddress), .in2(8'h50), .in3(adder_2_out), .out(multiplexer_3_out),
    .sel({mS1, mS0}));
  _8Reg44 u_8reg44_1 (.D(multiplexer_3_out), .CLR(in_4), .CLK(not_3_out), .Q(microMAR));
  not not_3 (not_3_out, CLK);
  ROM #(.dataWidth(16)) rom_1 (.addr(microMAR), .data(rom_1_data), .sel(1'b1));
  Hex_Digit_Display hex_digit_display_17 (.value(microMAR[3:0]));  // open: dp
  Hex_Digit_Display hex_digit_display_18 (.value(microMAR[7:4]));  // open: dp
  Register_part #(.width(16)) register_10 (
    .D(rom_1_data), .en(1'b1), .Q({CC6, CC5, CC4, CC3, CC2, CC1, CC0, MicroAddress, ADD}), .clk(CLK),
    .clr(1'b0));
  Adder adder_2 (
    .a({4'b0000, IR[15:12]}), .b({2'b00, IR5P, IR4P, IR3P, IR2P, IR1P, IR0P}), .out(adder_2_out), .cin(1'b0));  // open: cout
  and and_21 (and_21_out, IR[12], IR[13], IR[14], IR[15]);
  ROM #(.dataWidth(32)) rom_2 (.addr(microMAR), .data(rom_2_data), .sel(1'b1));
  Register_part #(.width(32)) register_11 (
    .D(rom_2_data), .en(1'b1),
    .Q({SUB, AND, OR, NOT, TCP, SHL, SHR, TRA1, PCtoB1, MBRtoB1, GPRStoB1, GPRTtoB1, UPIMMtoB1, TARGETtoB1, GPRStoB2, GPRTtoB2, SIMMtoB2, USIMMtoB2, _1toB2, B3toPC, B3toIR, B3toMAR, B3toMBR, B3toGPRD, B3toGPRT, B3toGPR2, MEMtoMBR, WRITE, INPUT, OUTPUT, ERROR, register_11_q[0]}),
    .clk(CLK), .clr(1'b0));
  and and_22 (IR0P, IR[0], and_21_out);
  and and_23 (IR1P, IR[1], and_21_out);
  and and_24 (IR2P, IR[2], and_21_out);
  and and_25 (IR3P, IR[3], and_21_out);
  and and_26 (IR4P, IR[4], and_21_out);
  and and_27 (IR5P, IR[5], and_21_out);

  // Other names for the same wires on the sheet: IR12_15[3:0] = IR[15:12]; BUS1[15:0] = out_8; BUS2[15:0] = out_7;
  //   BUS3[15:0] = out_10; SIGN = out_10[15]; RD[1:0] = IR[7:6]; RT[1:0] = IR[9:8]; RS[1:0] = IR[11:10];
  //   MEMOUT[15:0] = out_9; CLR = in_4; RESET = in_4; ZERO = out_12

  // Notes on the sheet:
  //   IR0-11
  //   contents of rom_1 (hex, n*v repeats v):
  //   2ee 2f4 2fa 300 2c8 2cc 2d0 2e0 2e8 306 30a 4*29e 2a8 2ac 2b0 2b4 2b8 2bc 2c0 2c4 17*29e 310 314 2d4
  //   2da 258 31a 31c 33*29e 0 1 0 400 1 2a1 0 2a0 0 2a0 0 2a0 0 2a0 0 2a0 0 2a0 0 2a0 1 2a1 0 2a0 0 2a0
  //   8d4 0 2a0 0 8dc 2a0 1 0 0 2a0 1 0 2a0 20a0 1 2a0 10a0 1 2a0 80a0 1 2a0 40a0 1 2a0 0 2a0 0 0 2a0 0
  //   2a0 0 0 2a0 2a0 2a0
  //   contents of rom_2 (hex, n*v repeats v):
  //   79*ffffd0 ffffd2 17ffbd0 7fcdf0 1bff7d0 ffffd0 defed0 deffd0 80defed0 80deffd0 40defed0 40deffd0
  //   20defed0 20deffd0 10fdfed0 10fdffd0 8fdfed0 8fdffd0 4dffed0 4dfffd0 2dffed0 2dfffd0 df7f50 df7fd0
  //   20dfbf50 20dfbfd0 1f7ff50 1f7ffd0 ffffd8 1fffed8 1ffffd8 1dfffd0 1dfffd4 ffffd0 df7bf0 fffdf0
  //   1bfff50 1bfffd0 df7bd0 1effdd0 ffffc0 80deffd0 7f6fd0 ffffd0 80deffd0 7f6fd0 ffffd0 1dfffd0 7f6fd0
  //   ffffd0 1dfffd0 7f6fd0 ffffd0 1fbefd0 ffffd0 17fff90 1fbefd0 ffffd0 1dfefd0 ffffd0 17fff90 1dfefd0
  //   ffffd0 ffffd0 ffffd0
endmodule

module Register (
  input  [15:0] D,
  input  CLK,
  input  CLR,
  output [15:0] Q
);

  wire not_1_out;

  Register_part #(.width(16)) register_1 (.D(D), .en(1'b1), .Q(Q), .clk(CLK), .clr(not_1_out));
  not not_1 (not_1_out, CLR);
endmodule

module Tri_State_Buffer (
  input  [15:0] in_1,
  input  in_2,
  output [15:0] out_3
);

  wire not_1_out;

  assign out_3 = not_1_out ? in_1 : 16'bz;  // Controlled_Buffer controlled_buffer_1
  not not_1 (not_1_out, in_2);
endmodule

module _8Reg44 (
  input  [7:0] D,
  input  CLR,
  input  CLK,
  output [7:0] Q
);

  wire CLR_t;

  not not_1 (CLR_t, CLR);
  D_Flip_Flop d_ff_1 (.clk(CLK), .D(D[0]), .Q(Q[0]), .preset(1'b0), .en(1'b1), .reset(CLR_t));  // open: Qn
  D_Flip_Flop d_ff_2 (.clk(CLK), .D(D[1]), .Q(Q[1]), .preset(1'b0), .en(1'b1), .reset(CLR_t));  // open: Qn
  D_Flip_Flop d_ff_3 (.clk(CLK), .D(D[2]), .Q(Q[2]), .preset(CLR_t), .en(1'b1), .reset(1'b0));  // open: Qn
  D_Flip_Flop d_ff_4 (.clk(CLK), .D(D[3]), .Q(Q[3]), .preset(CLR_t), .en(1'b1), .reset(1'b0));  // open: Qn
  D_Flip_Flop d_ff_5 (.clk(CLK), .D(D[4]), .Q(Q[4]), .preset(1'b0), .en(1'b1), .reset(CLR_t));  // open: Qn
  D_Flip_Flop d_ff_6 (.clk(CLK), .D(D[5]), .Q(Q[5]), .preset(CLR_t), .en(1'b1), .reset(1'b0));  // open: Qn
  D_Flip_Flop d_ff_7 (.clk(CLK), .D(D[6]), .Q(Q[6]), .preset(1'b0), .en(1'b1), .reset(CLR_t));  // open: Qn
  D_Flip_Flop d_ff_8 (.clk(CLK), .D(D[7]), .Q(Q[7]), .preset(1'b0), .en(1'b1), .reset(CLR_t));  // open: Qn
endmodule

module control (
  input  [15:0] in_1,
  input  SIGN,
  input  ZERO,
  input  in_4,
  input  START,
  input  DATA
);

  wire _1toB2, ADD, AND, and_1_out, and_2_out, and_3_out, and_4_out, and_5_out, and_6_out, and_7_out,
       and_8_out, B3toGPR2, B3toGPRD, B3toGPRT, B3toIR, B3toMAR, B3toMBR, B3toPC, bMicro, CC0, CC1, CC2, CC3,
       CC4, CC5, CC6, CLK, DATA_t, ERROR, GPRStoB1, GPRStoB2, GPRTtoB1, GPRTtoB2, INPUT, IR0P, IR1P, IR2P,
       IR3P, IR4P, IR5P, MBRtoB1, MEMtoMBR, mS0, mS1, NOT, not_1_out, OR, or_1_out, OUTPUT, PCtoB1, SHL, SHR,
       SIMMtoB2, START_t, SUB, TARGETtoB1, TCP, TRA1, UPIMMtoB1, USIMMtoB2, WRITE;
  wire [0:0] register_2_q;
  wire [7:0] adder_1_out, adder_2_out, MicroAddress, multiplexer_1_out, n8reg44_1_q;
  wire [15:0] rom_1_data;
  wire [31:0] rom_2_data;

  Clock #(.highDuration(100), .lowDuration(100)) clock_1 (.out(CLK));
  or or_1 (or_1_out, SIGN, ZERO);
  and and_1 (and_1_out, CC3, ~ZERO);  // AND_Gate
  and and_2 (and_2_out, CC4, ZERO);
  and and_3 (and_3_out, CC5, ~SIGN);  // AND_Gate
  and and_4 (and_4_out, CC6, or_1_out);
  and and_5 (and_5_out, ~START_t, bMicro);  // AND_Gate
  and and_6 (and_6_out, ~START_t, CC1);  // AND_Gate
  and and_7 (and_7_out, CC2, ~DATA_t);  // AND_Gate
  Adder adder_1 (.a(n8reg44_1_q), .b(8'h1), .out(adder_1_out), .cin(1'b0));  // open: cout
  or or_2 (mS1, START_t, CC1);
  or or_3 (mS0, and_5_out, and_6_out);
  or or_4 (bMicro, CC0, and_7_out, and_1_out, and_2_out, and_3_out, and_4_out);
  Multiplexer #(.select(2), .width(8), .enable("false")) multiplexer_1 (
    .in0(adder_1_out), .in1(MicroAddress), .in2(8'h50), .in3(adder_2_out), .out(multiplexer_1_out),
    .sel({mS1, mS0}));
  _8Reg44 u_8reg44_1 (.D(multiplexer_1_out), .CLR(in_4), .CLK(not_1_out), .Q(n8reg44_1_q));
  not not_1 (not_1_out, CLK);
  ROM #(.dataWidth(16)) rom_1 (.addr(n8reg44_1_q), .data(rom_1_data), .sel(1'b1));
  Hex_Digit_Display hex_digit_display_1 (.value(n8reg44_1_q[3:0]));  // open: dp
  Hex_Digit_Display hex_digit_display_2 (.value(n8reg44_1_q[7:4]));  // open: dp
  Register_part #(.width(16)) register_1 (
    .D(rom_1_data), .en(1'b1), .Q({CC6, CC5, CC4, CC3, CC2, CC1, CC0, MicroAddress, ADD}), .clk(CLK),
    .clr(1'b0));
  Adder adder_2 (
    .a({4'b0000, in_1[15:12]}), .b({2'b00, IR5P, IR4P, IR3P, IR2P, IR1P, IR0P}), .out(adder_2_out), .cin(1'b0));  // open: cout
  and and_8 (and_8_out, in_1[12], in_1[13], in_1[14], in_1[15]);
  ROM #(.dataWidth(32)) rom_2 (.addr(n8reg44_1_q), .data(rom_2_data), .sel(1'b1));
  Register_part #(.width(32)) register_2 (
    .D(rom_2_data), .en(1'b1),
    .Q({SUB, AND, OR, NOT, TCP, SHL, SHR, TRA1, PCtoB1, MBRtoB1, GPRStoB1, GPRTtoB1, UPIMMtoB1, TARGETtoB1, GPRStoB2, GPRTtoB2, SIMMtoB2, USIMMtoB2, _1toB2, B3toPC, B3toIR, B3toMAR, B3toMBR, B3toGPRD, B3toGPRT, B3toGPR2, MEMtoMBR, WRITE, INPUT, OUTPUT, ERROR, register_2_q[0]}),
    .clk(CLK), .clr(1'b0));
  and and_9 (IR0P, in_1[0], and_8_out);
  and and_10 (IR1P, in_1[1], and_8_out);
  and and_11 (IR2P, in_1[2], and_8_out);
  and and_12 (IR3P, in_1[3], and_8_out);
  and and_13 (IR4P, in_1[4], and_8_out);
  and and_14 (IR5P, in_1[5], and_8_out);

  // Other names for the same wires on the sheet: IR[15:0] = in_1; IR12_15[3:0] = in_1[15:12]; CLR = in_4;
  //   RESET = in_4

  // Notes on the sheet:
  //   IR0-11
  //   contents of rom_1 (hex, n*v repeats v):
  //   2ee 2f4 2fa 300 2c8 2cc 2d0 2e0 2e8 306 30a 4*29e 2a8 2ac 2b0 2b4 2b8 2bc 2c0 2c4 17*29e 310 314 2d4
  //   2da 258 31a 31c 33*29e 0 1 0 400 1 2a1 0 2a0 0 2a0 0 2a0 0 2a0 0 2a0 0 2a0 0 2a0 1 2a1 0 2a0 0 2a0
  //   8d4 0 2a0 0 8dc 2a0 1 0 0 2a0 1 0 2a0 20a0 1 2a0 10a0 1 2a0 80a0 1 2a0 40a0 1 2a0 0 2a0 0 0 2a0 0
  //   2a0 0 0 2a0 2a0 2a0
  //   contents of rom_2 (hex, n*v repeats v):
  //   79*ffffd0 ffffd2 17ffbd0 7fcdf0 1bff7d0 ffffd0 defed0 deffd0 80defed0 80deffd0 40defed0 40deffd0
  //   20defed0 20deffd0 10fdfed0 10fdffd0 8fdfed0 8fdffd0 4dffed0 4dfffd0 2dffed0 2dfffd0 df7f50 df7fd0
  //   20dfbf50 20dfbfd0 1f7ff50 1f7ffd0 ffffd8 1fffed8 1ffffd8 1dfffd0 1dfffd4 ffffd0 df7bf0 fffdf0
  //   1bfff50 1bfffd0 df7bd0 1effdd0 ffffc0 80deffd0 7f6fd0 ffffd0 80deffd0 7f6fd0 ffffd0 1dfffd0 7f6fd0
  //   ffffd0 1dfffd0 7f6fd0 ffffd0 1fbefd0 ffffd0 17fff90 1fbefd0 ffffd0 1dfefd0 ffffd0 17fff90 1dfefd0
  //   ffffd0 ffffd0 ffffd0
endmodule

module State_Machine (
  input  B,
  input  in_2,
  output out_3
);

  wire and_1_out, and_2_out, and_3_out, and_4_out, or_1_out, Q0, Q0N, Q1, Q1N;

  and and_1 (and_1_out, Q1N, Q0);
  and and_2 (and_2_out, B, Q1N);
  or or_1 (or_1_out, and_1_out, and_2_out);
  D_Flip_Flop D1 (.clk(in_2), .Q(Q1), .Qn(Q1N));  // open: D, preset, en, reset
  D_Flip_Flop D0 (.clk(in_2), .D(or_1_out), .Q(Q0), .Qn(Q0N));  // open: preset, en, reset
  and and_3 (and_3_out, Q1N, Q0N);
  and and_4 (and_4_out, Q1, Q0);
  or or_2 (out_3, and_3_out, and_4_out);
endmodule

module SyncButton (
  input  B,
  input  CLK,
  input  RESET,
  output OUT
);

  wire and_1_out, and_2_out, and_3_out, d_ff_1_q, d_ff_2_q, d_ff_2_qn, not_1_out, or_1_out;

  not not_1 (not_1_out, RESET);
  and and_1 (and_1_out, d_ff_1_q, ~d_ff_2_qn);  // AND_Gate
  and and_2 (and_2_out, ~B, d_ff_2_qn);  // AND_Gate
  and and_3 (and_3_out, ~B, ~d_ff_1_q, d_ff_2_qn);  // AND_Gate
  or or_1 (or_1_out, and_1_out, and_2_out);
  D_Flip_Flop d_ff_1 (.clk(CLK), .D(or_1_out), .Q(d_ff_1_q), .reset(not_1_out));  // open: Qn, preset, en
  D_Flip_Flop d_ff_2 (.clk(CLK), .D(and_3_out), .Q(d_ff_2_q), .Qn(d_ff_2_qn), .reset(not_1_out));  // open: preset, en
  and and_4 (OUT, d_ff_1_q, d_ff_2_q);
endmodule

module _2x4Dec (
  input  EN,
  input  [1:0] S,
  output Q0,
  output Q1,
  output Q2,
  output Q3
);

  wire decoder_1_out0, decoder_1_out1, decoder_1_out2, decoder_1_out3, not_1_out;

  not not_1 (not_1_out, EN);
  Decoder #(.select(2), .enable("false")) decoder_1 (
    .out0(decoder_1_out0), .out1(decoder_1_out1), .out2(decoder_1_out2), .out3(decoder_1_out3), .sel(S));
  nand nand_1 (Q0, not_1_out, decoder_1_out0);
  nand nand_2 (Q1, not_1_out, decoder_1_out1);
  nand nand_3 (Q3, decoder_1_out3, not_1_out);
  nand nand_4 (Q2, not_1_out, decoder_1_out2);
endmodule
